// Logisim project CPUseless.circ as structural Verilog: 2 circuits, main circuit main
module main (
  input  RegWrite,
  input  [7:0] PC_Adder,
  input  in_3,
  input  in_4,
  input  in_5,
  input  in_6,
  output [7:0] out_7,
  output [7:0] out_8,
  output [7:0] out_9,
  output [7:0] out_10,
  output [7:0] out_11,
  output [7:0] out_12
);

  wire and_1_out, and_2_out, and_3_out, and_4_out, Data_Clock_out, decoder_1_out0, decoder_1_out1,
       decoder_1_out2, decoder_1_out3, Instr_Clock_out, not_1_out, not_2_out, not_3_out;
  wire [7:0] adder_1_out, multiplexer_1_out, multiplexer_2_out, multiplexer_3_out, PC_q, X0_q, X1_q, X2_q,
       X3_q;

  Register PC (.D(adder_1_out), .clk(Instr_Clock_out), .Q(PC_q));  // open: en, clr
  Adder adder_1 (.a(PC_Adder), .b(PC_q), .out(adder_1_out));  // open: cin, cout
  Clock #(.highDuration(2), .lowDuration(2)) Instr_Clock (.out(Instr_Clock_out));
  not not_1 (not_1_out, in_4);
  RAM Instr_Memory (.addr(PC_q), .we(in_3), .oe(not_1_out), .clk(Instr_Clock_out), .dout(out_9));  // open: din
  Decoder #(.enable("false"), .select(2)) decoder_1 (
    .out0(decoder_1_out0), .out1(decoder_1_out1), .out2(decoder_1_out2), .out3(decoder_1_out3),
    .sel(out_9[5:4]));
  not not_2 (not_2_out, RegWrite);
  and and_1 (and_1_out, not_2_out, decoder_1_out0);
  and and_2 (and_2_out, not_2_out, decoder_1_out1);
  and and_3 (and_3_out, not_2_out, decoder_1_out2);
  and and_4 (and_4_out, not_2_out, decoder_1_out3);
  Register #(.trigger("falling")) X0 (
    .D(multiplexer_3_out), .en(and_1_out), .clk(Instr_Clock_out), .Q(X0_q));  // open: clr
  Register #(.trigger("falling")) X1 (
    .D(multiplexer_3_out), .en(and_2_out), .clk(Instr_Clock_out), .Q(X1_q));  // open: clr
  Register #(.trigger("falling")) X2 (
    .D(multiplexer_3_out), .en(and_3_out), .clk(Instr_Clock_out), .Q(X2_q));  // open: clr
  Register #(.trigger("falling")) X3 (
    .D(multiplexer_3_out), .en(and_4_out), .clk(Instr_Clock_out), .Q(X3_q));  // open: clr
  Hex_Digit_Display hex_digit_display_1 (.value(multiplexer_3_out[7:4]));  // open: dp
  Hex_Digit_Display ALU_Calculation (.value(multiplexer_3_out[3:0]));  // open: dp
  Multiplexer #(.select(2), .width(8)) multiplexer_1 (
    .in0(X0_q), .in1(X1_q), .in2(X2_q), .in3(X3_q), .out(multiplexer_1_out), .sel(out_9[3:2]));
  Multiplexer #(.select(2), .width(8)) multiplexer_2 (
    .in0(X0_q), .in1(X1_q), .in2(X2_q), .in3(X3_q), .out(multiplexer_2_out), .sel(out_9[1:0]));
  ALU alu_1 (.Input_A(multiplexer_1_out), .Input_B(multiplexer_2_out), .OPCODE(out_9[7:6]), .Arith_Output(out_7));
  Clock Data_Clock (.out(Data_Clock_out));
  RAM Data_Memory (.addr(out_7), .we(in_5), .oe(not_3_out), .clk(Data_Clock_out), .dout(out_10));  // open: din
  not not_3 (not_3_out, in_6);
  Multiplexer #(.width(8)) multiplexer_3 (.in0(out_7), .in1(out_10), .out(multiplexer_3_out), .sel(out_9[7]));

  assign out_8 = out_7;
  assign out_11 = out_9;
  assign out_12 = out_10;

  // Notes on the sheet:
  //   CPUseless!
  //   Dhihan`Ahmed
  //   Jesal`Gandhi
  //   I`pledge`my`honor`that`I`have`abided`by`the`Stevens`Honor`System`.
  //   Instuction_Memory
  //   Reg2
  //   Reg1
  //   Dest_Reg
  //   opcode
  //   ALU_Calculation
  //   Data_Memory
endmodule

module ALU (
  input  [7:0] Input_A,
  input  [7:0] Input_B,
  input  [1:0] OPCODE,
  output [7:0] Arith_Output
);

  wire [7:0] adder_1_out, subtractor_1_out;

  Adder adder_1 (.a(Input_A), .b(Input_B), .out(adder_1_out));  // open: cin, cout
  Subtractor subtractor_1 (.a(Input_A), .b(Input_B), .out(subtractor_1_out));  // open: bin, bout
  Multiplexer #(.select(2), .width(8)) multiplexer_1 (
    .in0(subtractor_1_out), .in1(adder_1_out), .in2(adder_1_out), .out(Arith_Output), .sel(OPCODE));  // open: in3
endmodule
